// Logisim project first.circ as structural Verilog: 1 circuit, main circuit main
module main (
  input  in_1,
  input  in_2,
  input  [7:0] in_3,
  input  [7:0] in_4,
  output out_5,
  output [7:0] out_6
);

  // Probe on in_3
  // Probe on in_4
  and and_1 (out_5, in_1, in_2);
  Adder adder_1 (.a(in_3), .b(in_4), .out(out_6));  // open: cin, cout
  // Probe on out_6
endmodule
