// Logisim project tutorial2.circ as structural Verilog: 1 circuit, main circuit main
module main (
  input  in_1
);

  wire undriven;
  wire [7:0] counter_1_q, ram_1_dout, ram_2_dout;

  Clock clock_1 ();  // open: out
  Counter counter_1 (.Q(counter_1_q), .clk(undriven));  // open: load, D, count, carry, up, clr
  RAM ram_1 (.addr(counter_1_q), .oe(in_1), .clk(undriven), .dout(ram_1_dout));  // open: we, din
  RAM ram_2 (.addr(counter_1_q), .oe(in_1), .clk(undriven), .dout(ram_2_dout));  // open: we, din
  Register register_1 (.D(ram_1_dout), .en(in_1), .clk(undriven));  // open: Q, clr
  Register register_2 (.D(ram_2_dout), .en(in_1), .clk(undriven));  // open: Q, clr
endmodule
